# Fritzing sketch MotorWiringDiagram (saved by Fritzing 1.0.4)
breadboards: 1

parts:
  Part1 = Motor Driver 1A Dual TB6612FNG
  M1 = DC Motor [voltage_(max)=6V voltage_(min)=3V]
  M2 = DC Motor [voltage_(max)=6V voltage_(min)=3V]
  VCC1 = 4 x AAA Battery Mount [internal_resistance=0.1Ω]
  Part2 = Arduino Uno (Rev3)
  VCC2 = Battery block 9V [internal_resistance=0.1Ω]  # not connected
  M3 = DC Motor [voltage_(max)=6V voltage_(min)=3V]  # not connected
  M4 = DC Motor [voltage_(max)=6V voltage_(min)=3V]  # not connected

nets:
  N1: Part1.B01, M2.pin_1
  N2: Part1.B02, M2.pin_2
  N3: Part1.A02, M1.pin_2
  N4: Part1.A01, M1.pin_1
  N5: Part1.GND, VCC1.-, Part2.D5_PWM
  N6: Part1.VM, VCC1.+
  N7: Part1.PWMA, Part2.GND
  N8: Part1.AIN2, Part2.D6_PWM
  N9: Part1.AIN1, Part2.D8
  N10: Part1.STBY, Part2.D7
  N11: Part1.BIN1, Part2.D9_PWM
  N12: Part1.BIN2, Part2.D2
  N13: Part1.PWMB, Part2.D4
